// Logisim project project233 Pipe.circ as structural Verilog: 5 circuits, main circuit Main
// x
module Main (
);

  wire and_1_out, Clk, comparator_1_eq, MemRead, MemWrite, or_1_out, RegWrite, ZeroFlag;
  wire [1:0] BusDSel, ForwardA, ForwardB, PcSrc, SelBusB;
  wire [4:0] aluOP, Imm5L, Imm16, multiplexer_2_out, RD2_q, RD3_q, RD4_q, rs1;
  wire [5:0] OpCode;
  wire [10:0] f;
  wire [19:0] adder_1_out, adder_3_out, BTA_q, Jump, multiplexer_1_out, NPA2_q, PC, PC___1;
  wire [31:0] ALUOut_q, ALURes, bit_extender_4_out, BusA, BusB, BusD, D_q, Imm11_5S, Imm16S, Imm16U, Imm_q,
       multiplexer_3_out, multiplexer_4_out, multiplexer_5_out, multiplexer_6_out, ram_1_data,
       register_1_out_7, register_1_out_8, rom_1_data, WBData;

  Clock clock_1 (.out(Clk));
  Register_part #(.width(20)) NPA2 (.D(PC___1), .en(1'b1), .Q(NPA2_q), .clk(Clk));  // open: clr
  Pcsrc_control pcsrc_control_1 (.out_3(PcSrc), .in_1(OpCode), .in_2(ZeroFlag));
  Adder #(.width(20)) adder_1 (.a(NPA2_q), .b(Imm11_5S[19:0]), .out(adder_1_out));  // open: cin, cout
  Control_Unit control_unit_1 (
    .in_1(OpCode), .out_3(BusDSel), .out_4(SelBusB), .out_5(aluOP), .out_6(MemRead), .out_7(MemWrite),
    .out_8(RegWrite), .in_2(f[3:0]));
  Register_part #(.width(20)) BTA (.D(adder_1_out), .Q(BTA_q), .clk(Clk));  // open: en, clr
  Multiplexer #(.select(2), .width(20), .enable("false")) multiplexer_1 (
    .in0(NPA2_q), .in1(Jump), .in2(BTA_q), .out(multiplexer_1_out), .sel(PcSrc));  // open: in3
  Register_part #(.width(20)) PC_reg (.D(multiplexer_1_out), .en(1'b1), .Q(PC), .clk(Clk));  // open: clr
  Adder #(.width(20)) adder_2 (.a(Imm16S[19:0]), .b(BusA[19:0]), .out(Jump));  // open: cin, cout
  Adder #(.width(20)) adder_3 (.a(20'h1), .b(PC), .out(adder_3_out));  // open: cin, cout
  Register_part #(.width(20)) NPA (.D(adder_3_out), .en(1'b1), .Q(PC___1), .clk(Clk));  // open: clr
  ROM #(.addrWidth(20), .dataWidth(32)) rom_1 (.addr(PC), .data(rom_1_data));  // open: sel
  Register_part #(.width(32)) Inst (
    .D(rom_1_data), .en(1'b1), .Q({f, Imm16, rs1, Imm5L, OpCode}), .clk(Clk));  // open: clr
  assign Imm16U = {{16{1'b0}}, {f, Imm16}};  // Bit_Extender bit_extender_1
  assign Imm16S = {{16{f[10]}}, {f, Imm16}};  // Bit_Extender bit_extender_2
  assign Imm11_5S = {{16{f[10]}}, {f, Imm5L}};  // Bit_Extender bit_extender_3
  Comparator #(.width(5), .mode("unsigned")) comparator_1 (
    .a({5{1'b0}}), .b(Imm5L), .eq(comparator_1_eq));  // open: gt, lt
  and and_1 (and_1_out, comparator_1_eq, PcSrc[0]);
  Multiplexer #(.width(5), .enable("false")) multiplexer_2 (
    .in0(Imm5L), .in1(PC___1[4:0]), .out(multiplexer_2_out), .sel(and_1_out));
  Multiplexer #(.select(2), .width(32), .enable("false")) multiplexer_3 (
    .in1(Imm16U), .in2(Imm16S), .in3(Imm11_5S), .out(multiplexer_3_out), .sel(SelBusB));  // open: in0
  Register_part #(.width(5)) RD2 (.D(multiplexer_2_out), .en(1'b1), .Q(RD2_q), .clk(Clk));  // open: clr
  Register register_1 (
    .in_3(RD4_q), .RegWr(RegWrite), .Clk(Clk), .out_7(register_1_out_7), .out_8(register_1_out_8),
    .in_4(rs1), .in_5(Imm16), .in_6(BusD));
  Register_part #(.width(32)) Imm (.D(multiplexer_3_out), .en(1'b1), .Q(Imm_q), .clk(Clk));  // open: clr
  Register_part #(.width(5)) RD3 (.D(RD2_q), .en(1'b1), .Q(RD3_q), .clk(Clk));  // open: clr
  Register_part #(.width(5)) RD4 (.D(RD3_q), .en(1'b1), .Q(RD4_q), .clk(Clk));  // open: clr
  Multiplexer #(.select(2), .width(32), .enable("false")) multiplexer_4 (
    .in0(register_1_out_7), .in1(ALURes), .in2(WBData), .in3(BusD), .out(multiplexer_4_out), .sel(ForwardA));
  Register_part #(.width(32)) u_BusA (.D(multiplexer_4_out), .en(1'b1), .Q(BusA), .clk(Clk));  // open: clr
  Multiplexer #(.select(2), .width(32), .enable("false")) multiplexer_5 (
    .in0(register_1_out_8), .in1(ALURes), .in2(WBData), .in3(BusD), .out(multiplexer_5_out), .sel(ForwardB));
  Register_part #(.width(32)) u_BusB (.D(multiplexer_5_out), .en(1'b1), .Q(BusB), .clk(Clk));  // open: clr
  or or_1 (or_1_out, SelBusB[1], SelBusB[0]);
  ALU alu_1 (.in_1(BusA), .in_2(multiplexer_6_out), .out_4(ZeroFlag), .in_3(aluOP), .out_5(ALURes));
  Multiplexer #(.width(32), .enable("false")) multiplexer_6 (
    .in0(BusB), .in1(Imm_q), .out(multiplexer_6_out), .sel(or_1_out));
  Register_part #(.width(32)) ALUOut (.D(ALURes), .en(1'b1), .Q(ALUOut_q), .clk(Clk));  // open: clr
  Register_part #(.width(32)) D (.D(BusB), .en(1'b1), .Q(D_q), .clk(Clk));  // open: clr
  RAM #(.addrWidth(20), .dataWidth(32), .bus("separate")) ram_1 (
    .addr(ALUOut_q[19:0]), .din(D_q), .data(ram_1_data), .str(MemWrite), .clk(Clk), .ld(MemRead));  // open: sel, clr
  assign bit_extender_4_out = {{12{1'b0}}, PC___1};  // Bit_Extender bit_extender_4
  Multiplexer #(.select(2), .width(32), .enable("false")) multiplexer_7 (
    .in0(ALUOut_q), .in1(ram_1_data), .in2(bit_extender_4_out), .out(WBData), .sel(BusDSel));  // open: in3
  Register_part #(.width(32)) Data (.D(WBData), .en(1'b1), .Q(BusD), .clk(Clk));  // open: clr

  // Other names for the same wires on the sheet: rs2[4:0] = Imm16; Imm11U[10:0] = f; Imm16[15:5] = f; Rd[4:0] = Imm5L

  // Notes on the sheet:
  //   PC src control
  //   Main control
  //   ExOP control
endmodule

// Reg
module Register (
  input  RegWr,
  input  Clk,
  input  [4:0] in_3,
  input  [4:0] in_4,
  input  [4:0] in_5,
  input  [31:0] in_6,
  output [31:0] out_7,
  output [31:0] out_8
);

  wire and_1_out, and_2_out, and_3_out, and_4_out, and_5_out, and_6_out, and_7_out, and_8_out, and_9_out,
       and_10_out, and_11_out, and_12_out, and_13_out, and_14_out, and_15_out, and_16_out, and_17_out,
       and_18_out, and_19_out, and_20_out, and_21_out, and_22_out, and_23_out, and_24_out, and_25_out,
       and_26_out, and_27_out, and_28_out, and_29_out, and_30_out, and_31_out, D1o01, D1o02, D1o03, D1o04,
       D1o05, D1o06, D1o07, D1o08, D1o09, D1o10, D1o11, D1o12, D1o13, D1o14, D1o15, D1o16, D1o17, D1o18,
       D1o19, D1o20, D1o21, D1o22, D1o23, D1o24, D1o25, D1o26, D1o27, D1o28, D1o29, D1o30, D1o31,
       decoder_2_out0, decoder_2_out1, decoder_2_out2, decoder_2_out3, decoder_2_out4, decoder_2_out5,
       decoder_2_out6, decoder_2_out7, decoder_2_out8, decoder_2_out9, decoder_2_out10, decoder_2_out11,
       decoder_2_out12, decoder_2_out13, decoder_2_out14, decoder_2_out15, decoder_2_out16, decoder_2_out17,
       decoder_2_out18, decoder_2_out19, decoder_2_out20, decoder_2_out21, decoder_2_out22, decoder_2_out23,
       decoder_2_out24, decoder_2_out25, decoder_2_out26, decoder_2_out27, decoder_2_out28, decoder_2_out29,
       decoder_2_out30, decoder_2_out31, decoder_3_out0, decoder_3_out1, decoder_3_out2, decoder_3_out3,
       decoder_3_out4, decoder_3_out5, decoder_3_out6, decoder_3_out7, decoder_3_out8, decoder_3_out9,
       decoder_3_out10, decoder_3_out11, decoder_3_out12, decoder_3_out13, decoder_3_out14, decoder_3_out15,
       decoder_3_out16, decoder_3_out17, decoder_3_out18, decoder_3_out19, decoder_3_out20, decoder_3_out21,
       decoder_3_out22, decoder_3_out23, decoder_3_out24, decoder_3_out25, decoder_3_out26, decoder_3_out27,
       decoder_3_out28, decoder_3_out29, decoder_3_out30, decoder_3_out31;
  wire [31:0] R1_q, R2_q, R3_q, R4_q, R5_q, R6_q, R7_q, R8_q, R9_q, R10_q, R11_q, R12_q, R13_q, R14_q, R15_q,
       R16_q, R17_q, R18_q, R19_q, R20_q, R21_q, R22_q, R23_q, R24_q, R25_q, R26_q, R27_q, R28_q, R29_q,
       R30_q, R31_q;

  Decoder #(.select(5), .enable("false")) decoder_1 (
    .out1(D1o01), .out2(D1o02), .out3(D1o03), .out4(D1o04), .out5(D1o05), .out6(D1o06), .out7(D1o07),
    .out8(D1o08), .out9(D1o09), .out10(D1o10), .out11(D1o11), .out12(D1o12), .out13(D1o13), .out14(D1o14),
    .out15(D1o15), .out16(D1o16), .out17(D1o17), .out18(D1o18), .out19(D1o19), .out20(D1o20), .out21(D1o21),
    .out22(D1o22), .out23(D1o23), .out24(D1o24), .out25(D1o25), .out26(D1o26), .out27(D1o27), .out28(D1o28),
    .out29(D1o29), .out30(D1o30), .out31(D1o31), .sel(in_3));  // open: out0
  and and_1 (and_1_out, D1o01, RegWr);
  and and_2 (and_2_out, D1o02, RegWr);
  and and_3 (and_3_out, D1o03, RegWr);
  and and_4 (and_4_out, D1o04, RegWr);
  and and_5 (and_5_out, D1o05, RegWr);
  and and_6 (and_6_out, D1o06, RegWr);
  and and_7 (and_7_out, D1o07, RegWr);
  and and_8 (and_8_out, D1o08, RegWr);
  and and_9 (and_9_out, D1o09, RegWr);
  and and_10 (and_10_out, D1o10, RegWr);
  and and_11 (and_11_out, D1o11, RegWr);
  and and_12 (and_12_out, D1o12, RegWr);
  and and_13 (and_13_out, D1o13, RegWr);
  and and_14 (and_14_out, D1o14, RegWr);
  and and_15 (and_15_out, D1o15, RegWr);
  and and_16 (and_16_out, D1o16, RegWr);
  and and_17 (and_17_out, D1o17, RegWr);
  and and_18 (and_18_out, D1o18, RegWr);
  and and_19 (and_19_out, D1o19, RegWr);
  and and_20 (and_20_out, D1o20, RegWr);
  and and_21 (and_21_out, D1o21, RegWr);
  and and_22 (and_22_out, D1o22, RegWr);
  and and_23 (and_23_out, D1o23, RegWr);
  and and_24 (and_24_out, D1o24, RegWr);
  and and_25 (and_25_out, D1o25, RegWr);
  and and_26 (and_26_out, D1o26, RegWr);
  and and_27 (and_27_out, D1o27, RegWr);
  and and_28 (and_28_out, D1o28, RegWr);
  and and_29 (and_29_out, D1o29, RegWr);
  and and_30 (and_30_out, D1o30, RegWr);
  and and_31 (and_31_out, D1o31, RegWr);
  Register_part #(.width(32)) R1 (.D(in_6), .en(and_1_out), .Q(R1_q), .clk(Clk));  // open: clr
  Register_part #(.width(32)) R2 (.D(in_6), .en(and_2_out), .Q(R2_q), .clk(Clk));  // open: clr
  Register_part #(.width(32)) R3 (.D(in_6), .en(and_3_out), .Q(R3_q), .clk(Clk));  // open: clr
  Register_part #(.width(32)) R4 (.D(in_6), .en(and_4_out), .Q(R4_q), .clk(Clk));  // open: clr
  Register_part #(.width(32)) R5 (.D(in_6), .en(and_5_out), .Q(R5_q), .clk(Clk));  // open: clr
  Register_part #(.width(32)) R6 (.D(in_6), .en(and_6_out), .Q(R6_q), .clk(Clk));  // open: clr
  Register_part #(.width(32)) R7 (.D(in_6), .en(and_7_out), .Q(R7_q), .clk(Clk));  // open: clr
  Register_part #(.width(32)) R8 (.D(in_6), .en(and_8_out), .Q(R8_q), .clk(Clk));  // open: clr
  Register_part #(.width(32)) R9 (.D(in_6), .en(and_9_out), .Q(R9_q), .clk(Clk));  // open: clr
  Register_part #(.width(32)) R10 (.D(in_6), .en(and_10_out), .Q(R10_q), .clk(Clk));  // open: clr
  Register_part #(.width(32)) R11 (.D(in_6), .en(and_11_out), .Q(R11_q), .clk(Clk));  // open: clr
  Register_part #(.width(32)) R12 (.D(in_6), .en(and_12_out), .Q(R12_q), .clk(Clk));  // open: clr
  Register_part #(.width(32)) R13 (.D(in_6), .en(and_13_out), .Q(R13_q), .clk(Clk));  // open: clr
  Register_part #(.width(32)) R14 (.D(in_6), .en(and_14_out), .Q(R14_q), .clk(Clk));  // open: clr
  Register_part #(.width(32)) R15 (.D(in_6), .en(and_15_out), .Q(R15_q), .clk(Clk));  // open: clr
  Register_part #(.width(32)) R16 (.D(in_6), .en(and_16_out), .Q(R16_q), .clk(Clk));  // open: clr
  Register_part #(.width(32)) R17 (.D(in_6), .en(and_17_out), .Q(R17_q), .clk(Clk));  // open: clr
  Register_part #(.width(32)) R18 (.D(in_6), .en(and_18_out), .Q(R18_q), .clk(Clk));  // open: clr
  Register_part #(.width(32)) R19 (.D(in_6), .en(and_19_out), .Q(R19_q), .clk(Clk));  // open: clr
  Register_part #(.width(32)) R20 (.D(in_6), .en(and_20_out), .Q(R20_q), .clk(Clk));  // open: clr
  Register_part #(.width(32)) R21 (.D(in_6), .en(and_21_out), .Q(R21_q), .clk(Clk));  // open: clr
  Register_part #(.width(32)) R22 (.D(in_6), .en(and_22_out), .Q(R22_q), .clk(Clk));  // open: clr
  Register_part #(.width(32)) R23 (.D(in_6), .en(and_23_out), .Q(R23_q), .clk(Clk));  // open: clr
  Register_part #(.width(32)) R24 (.D(in_6), .en(and_24_out), .Q(R24_q), .clk(Clk));  // open: clr
  Register_part #(.width(32)) R25 (.D(in_6), .en(and_25_out), .Q(R25_q), .clk(Clk));  // open: clr
  Register_part #(.width(32)) R26 (.D(in_6), .en(and_26_out), .Q(R26_q), .clk(Clk));  // open: clr
  Register_part #(.width(32)) R27 (.D(in_6), .en(and_27_out), .Q(R27_q), .clk(Clk));  // open: clr
  Register_part #(.width(32)) R28 (.D(in_6), .en(and_28_out), .Q(R28_q), .clk(Clk));  // open: clr
  Register_part #(.width(32)) R29 (.D(in_6), .en(and_29_out), .Q(R29_q), .clk(Clk));  // open: clr
  Register_part #(.width(32)) R30 (.D(in_6), .en(and_30_out), .Q(R30_q), .clk(Clk));  // open: clr
  Register_part #(.width(32)) R31 (.D(in_6), .en(and_31_out), .Q(R31_q), .clk(Clk));  // open: clr
  assign out_7 = decoder_2_out0 ? {32{1'b0}} : 32'bz;  // Controlled_Buffer controlled_buffer_1
  assign out_7 = decoder_2_out1 ? R1_q : 32'bz;  // Controlled_Buffer controlled_buffer_2
  assign out_7 = decoder_2_out2 ? R2_q : 32'bz;  // Controlled_Buffer controlled_buffer_3
  assign out_7 = decoder_2_out3 ? R3_q : 32'bz;  // Controlled_Buffer controlled_buffer_4
  assign out_7 = decoder_2_out4 ? R4_q : 32'bz;  // Controlled_Buffer controlled_buffer_5
  assign out_7 = decoder_2_out5 ? R5_q : 32'bz;  // Controlled_Buffer controlled_buffer_6
  assign out_7 = decoder_2_out6 ? R6_q : 32'bz;  // Controlled_Buffer controlled_buffer_7
  assign out_7 = decoder_2_out7 ? R7_q : 32'bz;  // Controlled_Buffer controlled_buffer_8
  assign out_7 = decoder_2_out8 ? R8_q : 32'bz;  // Controlled_Buffer controlled_buffer_9
  assign out_7 = decoder_2_out9 ? R9_q : 32'bz;  // Controlled_Buffer controlled_buffer_10
  assign out_7 = decoder_2_out10 ? R10_q : 32'bz;  // Controlled_Buffer controlled_buffer_11
  assign out_7 = decoder_2_out11 ? R11_q : 32'bz;  // Controlled_Buffer controlled_buffer_12
  assign out_7 = decoder_2_out12 ? R12_q : 32'bz;  // Controlled_Buffer controlled_buffer_13
  assign out_7 = decoder_2_out13 ? R13_q : 32'bz;  // Controlled_Buffer controlled_buffer_14
  assign out_7 = decoder_2_out14 ? R14_q : 32'bz;  // Controlled_Buffer controlled_buffer_15
  assign out_7 = decoder_2_out15 ? R15_q : 32'bz;  // Controlled_Buffer controlled_buffer_16
  assign out_7 = decoder_2_out16 ? R16_q : 32'bz;  // Controlled_Buffer controlled_buffer_17
  assign out_7 = decoder_2_out17 ? R17_q : 32'bz;  // Controlled_Buffer controlled_buffer_18
  assign out_7 = decoder_2_out18 ? R18_q : 32'bz;  // Controlled_Buffer controlled_buffer_19
  assign out_7 = decoder_2_out19 ? R19_q : 32'bz;  // Controlled_Buffer controlled_buffer_20
  assign out_7 = decoder_2_out20 ? R20_q : 32'bz;  // Controlled_Buffer controlled_buffer_21
  assign out_7 = decoder_2_out21 ? R21_q : 32'bz;  // Controlled_Buffer controlled_buffer_22
  assign out_7 = decoder_2_out22 ? R22_q : 32'bz;  // Controlled_Buffer controlled_buffer_23
  assign out_7 = decoder_2_out23 ? R23_q : 32'bz;  // Controlled_Buffer controlled_buffer_24
  assign out_7 = decoder_2_out24 ? R24_q : 32'bz;  // Controlled_Buffer controlled_buffer_25
  assign out_7 = decoder_2_out25 ? R25_q : 32'bz;  // Controlled_Buffer controlled_buffer_26
  assign out_7 = decoder_2_out26 ? R26_q : 32'bz;  // Controlled_Buffer controlled_buffer_27
  assign out_7 = decoder_2_out27 ? R27_q : 32'bz;  // Controlled_Buffer controlled_buffer_28
  assign out_7 = decoder_2_out28 ? R28_q : 32'bz;  // Controlled_Buffer controlled_buffer_29
  assign out_7 = decoder_2_out29 ? R29_q : 32'bz;  // Controlled_Buffer controlled_buffer_30
  assign out_7 = decoder_2_out30 ? R30_q : 32'bz;  // Controlled_Buffer controlled_buffer_31
  assign out_7 = decoder_2_out31 ? R31_q : 32'bz;  // Controlled_Buffer controlled_buffer_32
  Decoder #(.select(5), .enable("false")) decoder_2 (
    .out0(decoder_2_out0), .out1(decoder_2_out1), .out2(decoder_2_out2), .out3(decoder_2_out3),
    .out4(decoder_2_out4), .out5(decoder_2_out5), .out6(decoder_2_out6), .out7(decoder_2_out7),
    .out8(decoder_2_out8), .out9(decoder_2_out9), .out10(decoder_2_out10), .out11(decoder_2_out11),
    .out12(decoder_2_out12), .out13(decoder_2_out13), .out14(decoder_2_out14), .out15(decoder_2_out15),
    .out16(decoder_2_out16), .out17(decoder_2_out17), .out18(decoder_2_out18), .out19(decoder_2_out19),
    .out20(decoder_2_out20), .out21(decoder_2_out21), .out22(decoder_2_out22), .out23(decoder_2_out23),
    .out24(decoder_2_out24), .out25(decoder_2_out25), .out26(decoder_2_out26), .out27(decoder_2_out27),
    .out28(decoder_2_out28), .out29(decoder_2_out29), .out30(decoder_2_out30), .out31(decoder_2_out31),
    .sel(in_4));
  Decoder #(.select(5), .enable("false")) decoder_3 (
    .out0(decoder_3_out0), .out1(decoder_3_out1), .out2(decoder_3_out2), .out3(decoder_3_out3),
    .out4(decoder_3_out4), .out5(decoder_3_out5), .out6(decoder_3_out6), .out7(decoder_3_out7),
    .out8(decoder_3_out8), .out9(decoder_3_out9), .out10(decoder_3_out10), .out11(decoder_3_out11),
    .out12(decoder_3_out12), .out13(decoder_3_out13), .out14(decoder_3_out14), .out15(decoder_3_out15),
    .out16(decoder_3_out16), .out17(decoder_3_out17), .out18(decoder_3_out18), .out19(decoder_3_out19),
    .out20(decoder_3_out20), .out21(decoder_3_out21), .out22(decoder_3_out22), .out23(decoder_3_out23),
    .out24(decoder_3_out24), .out25(decoder_3_out25), .out26(decoder_3_out26), .out27(decoder_3_out27),
    .out28(decoder_3_out28), .out29(decoder_3_out29), .out30(decoder_3_out30), .out31(decoder_3_out31),
    .sel(in_5));
  assign out_8 = decoder_3_out0 ? {32{1'b0}} : 32'bz;  // Controlled_Buffer controlled_buffer_33
  assign out_8 = decoder_3_out1 ? R1_q : 32'bz;  // Controlled_Buffer controlled_buffer_34
  assign out_8 = decoder_3_out2 ? R2_q : 32'bz;  // Controlled_Buffer controlled_buffer_35
  assign out_8 = decoder_3_out3 ? R3_q : 32'bz;  // Controlled_Buffer controlled_buffer_36
  assign out_8 = decoder_3_out4 ? R4_q : 32'bz;  // Controlled_Buffer controlled_buffer_37
  assign out_8 = decoder_3_out5 ? R5_q : 32'bz;  // Controlled_Buffer controlled_buffer_38
  assign out_8 = decoder_3_out6 ? R6_q : 32'bz;  // Controlled_Buffer controlled_buffer_39
  assign out_8 = decoder_3_out7 ? R7_q : 32'bz;  // Controlled_Buffer controlled_buffer_40
  assign out_8 = decoder_3_out8 ? R8_q : 32'bz;  // Controlled_Buffer controlled_buffer_41
  assign out_8 = decoder_3_out9 ? R9_q : 32'bz;  // Controlled_Buffer controlled_buffer_42
  assign out_8 = decoder_3_out10 ? R10_q : 32'bz;  // Controlled_Buffer controlled_buffer_43
  assign out_8 = decoder_3_out11 ? R11_q : 32'bz;  // Controlled_Buffer controlled_buffer_44
  assign out_8 = decoder_3_out12 ? R12_q : 32'bz;  // Controlled_Buffer controlled_buffer_45
  assign out_8 = decoder_3_out13 ? R13_q : 32'bz;  // Controlled_Buffer controlled_buffer_46
  assign out_8 = decoder_3_out14 ? R14_q : 32'bz;  // Controlled_Buffer controlled_buffer_47
  assign out_8 = decoder_3_out15 ? R15_q : 32'bz;  // Controlled_Buffer controlled_buffer_48
  assign out_8 = decoder_3_out16 ? R16_q : 32'bz;  // Controlled_Buffer controlled_buffer_49
  assign out_8 = decoder_3_out17 ? R17_q : 32'bz;  // Controlled_Buffer controlled_buffer_50
  assign out_8 = decoder_3_out18 ? R18_q : 32'bz;  // Controlled_Buffer controlled_buffer_51
  assign out_8 = decoder_3_out19 ? R19_q : 32'bz;  // Controlled_Buffer controlled_buffer_52
  assign out_8 = decoder_3_out20 ? R20_q : 32'bz;  // Controlled_Buffer controlled_buffer_53
  assign out_8 = decoder_3_out21 ? R21_q : 32'bz;  // Controlled_Buffer controlled_buffer_54
  assign out_8 = decoder_3_out22 ? R22_q : 32'bz;  // Controlled_Buffer controlled_buffer_55
  assign out_8 = decoder_3_out23 ? R23_q : 32'bz;  // Controlled_Buffer controlled_buffer_56
  assign out_8 = decoder_3_out24 ? R24_q : 32'bz;  // Controlled_Buffer controlled_buffer_57
  assign out_8 = decoder_3_out25 ? R25_q : 32'bz;  // Controlled_Buffer controlled_buffer_58
  assign out_8 = decoder_3_out26 ? R26_q : 32'bz;  // Controlled_Buffer controlled_buffer_59
  assign out_8 = decoder_3_out27 ? R27_q : 32'bz;  // Controlled_Buffer controlled_buffer_60
  assign out_8 = decoder_3_out28 ? R28_q : 32'bz;  // Controlled_Buffer controlled_buffer_61
  assign out_8 = decoder_3_out29 ? R29_q : 32'bz;  // Controlled_Buffer controlled_buffer_62
  assign out_8 = decoder_3_out30 ? R30_q : 32'bz;  // Controlled_Buffer controlled_buffer_63
  assign out_8 = decoder_3_out31 ? R31_q : 32'bz;  // Controlled_Buffer controlled_buffer_64

  // Other names for the same wires on the sheet: BusA[31:0] = out_7; BusB[31:0] = out_8; BusD[31:0] = in_6;
  //   Ra[4:0] = in_4; Rb[4:0] = in_5; RD[4:0] = in_3
endmodule

module ALU (
  input  [31:0] in_1,
  input  [31:0] in_2,
  input  [4:0] in_3,
  output out_4,
  output [31:0] out_5
);

  wire Borrow, comparator_1_lt, comparator_2_lt, Overflow;
  wire [31:0] adder_1_out, and_1_out, bit_extender_1_out, bit_extender_2_out, multiplexer_1_out,
       multiplier_1_out, not_1_out, or_1_out, shifter_1_out, shifter_2_out, shifter_3_out, shifter_4_out,
       shifter_5_out, subtractor_1_out, xor_1_out;

  Shifter #(.width(32)) shifter_1 (.in(in_1), .\dist (in_2[4:0]), .out(shifter_1_out));
  Shifter #(.width(32), .shift("lr")) shifter_2 (.in(in_1), .\dist (in_2[4:0]), .out(shifter_2_out));
  Shifter #(.width(32), .shift("ar")) shifter_3 (.in(in_1), .\dist (in_2[4:0]), .out(shifter_3_out));
  Shifter #(.width(32), .shift("rr")) shifter_4 (.in(in_1), .\dist (in_2[4:0]), .out(shifter_4_out));
  assign and_1_out = in_1 & in_2;  // AND_Gate and_1, 32 bits wide
  assign or_1_out = in_1 | in_2;  // OR_Gate or_1, 32 bits wide
  assign xor_1_out = in_1 ^ in_2;  // XOR_Gate xor_1, 32 bits wide
  Adder #(.width(32)) adder_1 (.a(in_1), .b(in_2), .out(adder_1_out), .cout(Overflow));  // open: cin
  Subtractor #(.width(32)) subtractor_1 (.a(in_1), .b(in_2), .out(subtractor_1_out), .bout(Borrow));  // open: bin
  Comparator #(.width(32), .mode("unsigned")) comparator_1 (.a(in_1), .b(in_2), .lt(comparator_1_lt));  // open: gt, eq
  Comparator #(.width(32)) comparator_2 (.a(in_1), .b(in_2), .lt(comparator_2_lt));  // open: gt, eq
  assign not_1_out = ~or_1_out;  // NOT_Gate not_1, 32 bits wide
  Shifter #(.width(32)) shifter_5 (.in(in_1), .\dist (5'b10000), .out(shifter_5_out));
  Multiplier #(.width(32)) multiplier_1 (.a(in_1), .b(in_2), .out(multiplier_1_out));  // open: cin, cout
  assign bit_extender_1_out = {{31{1'b0}}, comparator_1_lt};  // Bit_Extender bit_extender_1
  assign bit_extender_2_out = {{31{1'b0}}, comparator_2_lt};  // Bit_Extender bit_extender_2
  Multiplexer #(.width(32), .enable("false")) multiplexer_1 (
    .in0(shifter_5_out), .in1(multiplier_1_out), .out(multiplexer_1_out), .sel(in_3[4]));
  Multiplexer #(.select(4), .width(32), .disabled(0), .enable("false")) multiplexer_2 (
    .in0(shifter_1_out), .in1(shifter_2_out), .in2(shifter_3_out), .in3(shifter_4_out), .in4(adder_1_out),
    .in5(subtractor_1_out), .in6(bit_extender_1_out), .in7(bit_extender_2_out), .in8(and_1_out),
    .in9(or_1_out), .in10(not_1_out), .in11(xor_1_out), .in12(multiplexer_1_out), .in14(adder_1_out),
    .in15(adder_1_out), .out(out_5), .sel(in_3[3:0]));  // open: in13
  Comparator #(.width(32), .mode("unsigned")) comparator_3 (.a(out_5), .b({32{1'b0}}), .eq(out_4));  // open: gt, lt

  // Other names for the same wires on the sheet: ALU_result[31:0] = out_5; ALUop[4:0] = in_3; BusA[31:0] = in_1;
  //   BusB[31:0] = in_2; Zero_Flag = out_4
endmodule

// Main control
module Control_Unit (
  input  [5:0] in_1,
  input  [3:0] in_2,
  output [1:0] out_3,
  output [1:0] out_4,
  output [4:0] out_5,
  output out_6,
  output out_7,
  output out_8
);

  wire comparator_1_eq, comparator_2_eq;
  wire [4:0] adder_1_out, adder_2_out, adder_3_out, bit_extender_1_out, bit_extender_2_out,
       bit_extender_3_out, bit_extender_4_out, bit_extender_5_out, multiplexer_1_out, rom_2_data;
  wire [5:0] bit_extender_6_out;

  ROM #(.addrWidth(6), .dataWidth(7)) rom_1 (.addr(in_1), .data({out_8, out_4, out_7, out_6, out_3}));  // open: sel
  ROM #(.addrWidth(6), .dataWidth(5)) rom_2 (.addr(in_1), .data(rom_2_data));  // open: sel
  assign bit_extender_1_out = {{4{1'b0}}, rom_2_data[1]};  // Bit_Extender bit_extender_1
  assign bit_extender_2_out = {{1{1'b1}}, in_2};  // Bit_Extender bit_extender_2
  Adder #(.width(5)) adder_1 (.a(5'b00101), .b(bit_extender_1_out), .out(adder_1_out));  // open: cin, cout
  Adder #(.width(5)) adder_2 (.a(adder_1_out), .b(bit_extender_3_out), .out(adder_2_out));  // open: cin, cout
  assign bit_extender_3_out = {{4{1'b0}}, rom_2_data[2]};  // Bit_Extender bit_extender_3
  assign bit_extender_4_out = {{1{1'b0}}, rom_2_data[3:0]};  // Bit_Extender bit_extender_4
  Comparator #(.width(4), .mode("unsigned")) comparator_1 (
    .a(rom_2_data[3:0]), .b(4'b1100), .eq(comparator_1_eq));  // open: gt, lt
  assign bit_extender_5_out = {{4{1'b0}}, comparator_1_eq};  // Bit_Extender bit_extender_5
  assign bit_extender_6_out = {{5{1'b0}}, 1'b0};  // Bit_Extender bit_extender_6
  Adder #(.width(5)) adder_3 (.a(bit_extender_4_out), .b(bit_extender_5_out), .out(adder_3_out));  // open: cin, cout
  Comparator #(.width(6), .mode("unsigned")) comparator_2 (
    .a(bit_extender_6_out), .b(in_1), .eq(comparator_2_eq));  // open: gt, lt
  Multiplexer #(.width(5), .enable("false")) multiplexer_1 (
    .in0(adder_3_out), .in1(adder_2_out), .out(multiplexer_1_out), .sel(rom_2_data[4]));
  Multiplexer #(.width(5), .enable("false")) multiplexer_2 (
    .in0(multiplexer_1_out), .in1(bit_extender_2_out), .out(out_5), .sel(comparator_2_eq));

  // Other names for the same wires on the sheet: BusWrite[1:0] = out_3; MemRead = out_6; MemWrite = out_7;
  //   SelBusB[1:0] = out_4; RegWrite = out_8; aluOP[4:0] = out_5; f[3:0] = in_2; OpCode[5:0] = in_1
endmodule

// PCsrc control
module Pcsrc_control (
  input  [5:0] in_1,
  input  in_2,
  output [1:0] out_3
);

  wire xor_1_out;

  and and_1 (out_3[0], in_1[3], in_1[2], in_1[0]);
  xor xor_1 (xor_1_out, in_1[0], in_2);
  and and_2 (out_3[1], xor_1_out, in_1[4]);

  // Other names for the same wires on the sheet: OpCode[5:0] = in_1; PcSrc[1:0] = out_3; ZeroFlag = in_2
endmodule
